# Fritzing sketch DIY Arduino (saved by Fritzing 0.9.0b)
breadboards: 1

parts:
  U1 = atmega328 [package=dip]
  XTAL1 = Crystal [frequency="16 Mhz" package=THT]
  C2 = Capacitor [package=cap-pth-small2]
  C1 = Capacitor [package=cap-pth-small2]
  IC1 = Voltage Regulator [package=to-220-alt]
  VCC1 = Battery block 9V
  R1 = Resistor [tolerance=±5% resistance=100 package=THT]
  S2 = Pushbutton [package=THT]

nets:
  N1: U1.RESET, R1.Pin_1, S2.leg0
  N2: U1.XLAT1, XTAL1.pin_1, C1.1
  N3: U1.XLAT2, XTAL1.pin_0, C2.2
  N4: U1.AVCC, IC1.OUT
  N5: U1.GND#21, IC1.IN, VCC1.-
  N6: C2.1, C1.2, S2.leg1
  N7: IC1.GND, VCC1.+
