# Fritzing sketch Kumanda (saved by Fritzing 0.9.0b)
breadboards: 1

parts:
  U1 = atmega328 [package=dip]
  XTAL1 = Crystal [frequency="16 Mhz" package=THT]
  C2 = Capacitor [package=cap-pth-small2]
  C1 = Capacitor [package=cap-pth-small2]
  IC1 = Voltage Regulator [package=to-220-alt]
  R1 = Resistor [tolerance=±5% resistance=100 package=THT]
  S2 = Pushbutton [package=THT]
  S3 = Pushbutton [package=THT]
  S4 = Pushbutton [package=THT]
  S5 = Pushbutton [package=THT]
  S6 = Pushbutton [package=THT]
  R2 = Resistor [tolerance=±5% resistance=220 package=THT]
  R3 = Resistor [tolerance=±5% resistance=220 package=THT]
  R4 = Resistor [tolerance=±5% resistance=220 package=THT]
  R5 = Resistor [tolerance=±5% resistance=220 package=THT]
  IR1 = TSOP312.., 314.. [package=THT]
  LED2 = smd LED [color="Infrared (940nm)" package="1206 [SMD]"]
  SG1 = Buzzer 12mm [package=buzzer-ccv]
  U2 = SWITCH_SPDT [package=kps-1290]
  R6 = Resistor [tolerance=±5% resistance=220 package=THT]
  LED3 = smd LED [color="Red (633nm)" package="1206 [SMD]"]
  LED4 = smd LED [color="Green (565nm)" package="1206 [SMD]"]
  LED5 = smd LED [color="Yellow (585nm)" package="1206 [SMD]"]
  R7 = Resistor [tolerance=±5% resistance=220 package=THT]
  R8 = Resistor [tolerance=±5% resistance=220 package=THT]
  R9 = Resistor [tolerance=±5% resistance=220 package=THT]
  S7 = Pushbutton [package=THT]
  R10 = Resistor [tolerance=±5% resistance=220 package=THT]
  R11 = Resistor [tolerance=±5% resistance=220 package=THT]
  LED6 = smd LED [color="Blue (470nm)" package="1206 [SMD]"]
  R12 = Rotary Potentiometer (Small) [maximum_resistance=100kΩ package=THT]
  BAT1 = BC9VPC [package=bc9vpc]

nets:
  N1: U1.RESET, R1.Pin_1, S2.leg0
  N2: U1.D0_(RX), S7.leg0, R10.Pin_1
  N3: U1.D2, IR1.Data
  N4: U1.D3_(PWM), LED2.anode
  N5: U1.D4, SG1.1
  N6: U1.VCC, R1.Pin_0, S3.leg1, S4.leg1, S5.leg1, S6.leg1, S7.leg1
  N7: U1.GND#7, C2.1, C1.2, S2.leg1, R2.Pin_0, R3.Pin_0, R4.Pin_0, R5.Pin_0, R7.Pin_0, R8.Pin_0, R9.Pin_0, R10.Pin_0, R11.Pin_0
  N8: U1.XLAT1, XTAL1.pin_1, C1.1
  N9: U1.XLAT2, XTAL1.pin_0
  N10: U1.D5_(PWM), S6.leg0, R5.Pin_1
  N11: U1.D6_(PWM), S5.leg0, R4.Pin_1
  N12: U1.D7, S4.leg0, R3.Pin_1
  N13: U1.D8, S3.leg0, R2.Pin_1
  N14: U1.D9_(PWM), U2.P
  N15: U1.D10_(PWM), LED3.anode
  N16: U1.D11_(PWM), LED4.anode
  N17: U1.D12, LED5.anode
  N18: U1.AVCC, U1.A5, IC1.OUT, IR1.Vs, U2.O, R12.leg2
  N19: U1.GND#21, IC1.IN, IR1.GND, SG1.2, U2.S, R6.Pin_0, R12.leg1, BAT1.V-
  N20: U1.A0, LED6.anode, R12.wiper
  N21: IC1.GND, BAT1.V+
  N22: LED2.cathode, R6.Pin_1
  N23: LED3.cathode, R7.Pin_1
  N24: LED4.cathode, R8.Pin_1
  N25: LED5.cathode, R9.Pin_1
  N26: R11.Pin_1, LED6.cathode
